# Fritzing sketch esc_fritzing (saved by Fritzing 0.9.3b)
circuit board: 2.95393cm x 1.47172cm

parts:
  M = MOSFET-PCHANNEL [package=sot23-3]
  D1 = DIODE-SCHOTTKY [package=sma-diode]
  C2 = Capacitor Polarized [package=panasonic_d]
  2 = Resistor [tolerance=±5% resistance=220 package="0603 [SMD]"]
  k = Resistor [tolerance=±5% resistance=220 package="0603 [SMD]"]
  + = Header 1 [package=luxeon-pad]
  - = Header 1 [package=luxeon-pad]
  V++ = Header 1 [package=luxeon-pad]
  G = Header 1 [package=luxeon-pad]
  S = Header 1 [package=luxeon-pad]

nets:
  N1: M.G, 2.Pin_1, k.Pin_0
  N2: M.S, k.Pin_1, G.1
  N3: M.D, D1.C, C2.-, -.1
  N4: D1.A, C2.+, +.1, V++.1
  N5: 2.Pin_0, S.1
